# Fritzing sketch led (saved by Fritzing 0.9.6b)
breadboards: 1

parts:
  GPIO_27 = Raspberry Pi 4B
  R3 = Resistor [tolerance=±5% power=0.25 resistance=220 package=THT]
  LED1 = smd LED [color="Red (633nm)" current=0.030 package="0805 [SMD]"]

nets:
  N1: GPIO_27.GPIO27, LED1.anode
  N2: GPIO_27.GND, R3.Pin_0
  N3: R3.Pin_1, LED1.cathode
