# Fritzing sketch Phase2 (saved by Fritzing 0.9.3b)
breadboards: 1

parts:
  J1 = T Cobbler Plus
  LED1 = LED - 3mm [color="Red (633nm)" package="3 mm [THT]"]
  RHT1 = Humidity and Temperature Sensor RHT03
  R2 = Resistor [tolerance=±5% resistance=220 package="0603 [SMD]"]
  R3 = Resistor [tolerance=±5% resistance=220 package="0603 [SMD]"]

nets:
  N1: J1.GND#8, RHT1.GND_2, R3.Pin_1
  N2: J1.#17, RHT1.GND_1
  N3: J1.#27, LED1.cathode
  3.3V: J1.3.3V, RHT1.Vcc, R2.Pin_0
  N4: LED1.anode, R3.Pin_0
  N5: RHT1.Data-signal, R2.Pin_1

custom parts:
  T Cobbler Plus: The T-Cobbler Plus is an add on prototyping board from Adafruit specifically designed for the Raspberry Pi B+ that can break out all those tasty power, GPIO, I2C and SPI pins from the 40-pin header onto a solderless breadboard. This set will make "cobbling together" prototypes with the Pi super easy. The T-Cobbler Plus can plug into any solderless breadboard.
