# Fritzing sketch Phase3 (saved by Fritzing 0.9.6b)
breadboards: 1

parts:
  J1 = T Cobbler Plus
  LED1 = LED - 3mm [color="Red (633nm)" current=0.030 package="3 mm [THT]"]
  RHT1 = Humidity and Temperature Sensor RHT03
  R2 = Resistor [tolerance=±5% resistance=220 package="0603 [SMD]"]
  R3 = Resistor [tolerance=±5% resistance=220 package="0603 [SMD]"]
  M3 = DC Motor
  U3 = LIPO-1000mAh [package=lipo-1000]  # not connected
  IC2 = L293D [package=THT]

nets:
  N1: J1.5.0V#1, IC2.+V
  N2: J1.GND#8, RHT1.GND_2, R3.Pin_1, IC2.0V
  N3: J1.#17, RHT1.GND_1
  N4: J1.#27, LED1.cathode
  3.3V: J1.3.3V, RHT1.Vcc, R2.Pin_0
  N5: J1.#6, IC2.Enable_1
  N6: J1.#13, IC2.In_1
  N7: LED1.anode, R3.Pin_0
  N8: RHT1.Data-signal, R2.Pin_1
  N9: M3.pin_1, IC2.Out_1_(_Controlled_by_Enable_1_)
  N10: M3.pin_2, IC2.Out_2_(_Controlled_by_Enable_1_)

custom parts:
  T Cobbler Plus: The T-Cobbler Plus is an add on prototyping board from Adafruit specifically designed for the Raspberry Pi B+ that can break out all those tasty power, GPIO, I2C and SPI pins from the 40-pin header onto a solderless breadboard. This set will make "cobbling together" prototypes with the Pi super easy. The T-Cobbler Plus can plug into any solderless breadboard.
